// Logisim project 4-function-calculator.circ as structural Verilog: 1 circuit, main circuit main
module main (
  input  [3:0] A,
  input  [1:0] in_2,
  input  [3:0] B,
  output [3:0] out_4
);

  wire [1:0] bitselector_1_out;
  wire [3:0] adder_1_out, multiplier_1_out, shifter_1_out, subtractor_1_out;

  BitSelector #(.width(4), .group(2)) bitselector_1 (.in(B), .out(bitselector_1_out), .sel(1'b0));
  Adder #(.width(4)) adder_1 (.a(A), .b(B), .out(adder_1_out));  // open: cin, cout
  Subtractor #(.width(4)) subtractor_1 (.a(A), .b(B), .out(subtractor_1_out));  // open: bin, bout
  Multiplier #(.width(4)) multiplier_1 (.a(B), .b(A), .out(multiplier_1_out));  // open: cin, cout
  Shifter #(.width(4)) shifter_1 (.in(A), .\dist (bitselector_1_out), .out(shifter_1_out));
  // Probe on out_4
  Multiplexer #(.select(2), .width(4), .enable("false")) multiplexer_1 (
    .in0(adder_1_out), .in1(subtractor_1_out), .in2(multiplier_1_out), .in3(shifter_1_out), .out(out_4),
    .sel(in_2));
endmodule
