// Logisim project cpu.circ as structural Verilog: 7 circuits, main circuit CPU
module CPU (
  output [7:0] PC
);

  wire alu_1_zero_dectector, clock_1_out, multiplexer_1_out;
  wire [1:0] instruction_decoder_1_rd, instruction_decoder_1_rs, instruction_decoder_1_rt, multiplexer_3_out;
  wire [3:0] display_driver_1_hex0, display_driver_1_hex1;
  wire [7:0] alu_1_result, instruction_decoder_1_immediate, multiplexer_2_out, multiplexer_4_out, ram_1_data,
       Random_result, register_file_1_read_data_1, register_file_1_read_data_2;
  wire [15:0] rom_1_data;

  PC u_PC (
    .Output(PC), .Clock(multiplexer_1_out), .IMM(instruction_decoder_1_immediate),
    .Zero(alu_1_zero_dectector), .Branch_Instruction(1'b0), .Jump(1'b0));
  Multiplexer #(.enable("false")) multiplexer_1 (.in0(clock_1_out), .in1(1'b0), .out(multiplexer_1_out), .sel(1'b0));
  Clock clock_1 (.out(clock_1_out));
  Instruction_Decoder instruction_decoder_1 (
    .Instruction(rom_1_data), .RS(instruction_decoder_1_rs), .RT(instruction_decoder_1_rt),
    .RD(instruction_decoder_1_rd), .Immediate(instruction_decoder_1_immediate));  // open: Opcode
  ROM #(.dataWidth(16)) rom_1 (.addr(PC), .data(rom_1_data));  // open: sel
  Random Random (.Clock(multiplexer_1_out), .RS(register_file_1_read_data_1), .Result(Random_result));
  Multiplexer #(.select(2), .width(8), .enable("false")) multiplexer_2 (
    .in0(Random_result), .in1(ram_1_data), .in2(alu_1_result), .out(multiplexer_2_out));  // open: in3, sel
  Multiplexer #(.width(2), .enable("false")) multiplexer_3 (
    .in0(instruction_decoder_1_rt), .in1(instruction_decoder_1_rd), .out(multiplexer_3_out));  // open: sel
  Register_File register_file_1 (
    .Write_Data(multiplexer_2_out), .Read_Data_1(register_file_1_read_data_1),
    .Read_Register_1(instruction_decoder_1_rs), .Read_Data_2(register_file_1_read_data_2),
    .Read_Register_2(instruction_decoder_1_rt), .Clock(multiplexer_1_out), .Write_Address(multiplexer_3_out));  // open: Write_Enable
  Multiplexer #(.width(8), .enable("false")) multiplexer_4 (
    .in0(register_file_1_read_data_2), .in1(instruction_decoder_1_immediate), .out(multiplexer_4_out));  // open: sel
  ALU alu_1 (
    .Operand_A(register_file_1_read_data_1), .Operand_B(multiplexer_4_out), .Result(alu_1_result),
    .Zero_Dectector(alu_1_zero_dectector));  // open: Branch, Operation_Select
  Display_Driver display_driver_1 (
    .Put_Data(register_file_1_read_data_1), .Clock(multiplexer_1_out), .Hex0(display_driver_1_hex0),
    .Hex1(display_driver_1_hex1));  // open: Put_Enable
  Hex_Digit_Display hex_digit_display_1 (.value(display_driver_1_hex1));  // open: dp
  Hex_Digit_Display hex_digit_display_2 (.value(display_driver_1_hex0));  // open: dp
  RAM #(.bus("separate")) ram_1 (
    .addr(alu_1_result), .din(register_file_1_read_data_2), .data(ram_1_data), .clk(multiplexer_1_out));  // open: str, sel, ld, clr
endmodule

module Instruction_Decoder (
  input  [15:0] Instruction,
  output [3:0] Opcode,
  output [1:0] RS,
  output [1:0] RT,
  output [1:0] RD,
  output [7:0] Immediate
);


  assign Immediate = Instruction[7:0];
  assign Opcode = Instruction[15:12];
  assign RD = Instruction[7:6];
  assign RS = Instruction[11:10];
  assign RT = Instruction[9:8];
endmodule

module Register_File (
  input  [7:0] Write_Data,
  input  Clock,
  input  Write_Enable,
  input  [1:0] Read_Register_1,
  input  [1:0] Write_Address,
  input  [1:0] Read_Register_2,
  output [7:0] Read_Data_1,
  output [7:0] Read_Data_2
);

  wire and_1_out, and_2_out, and_3_out, and_4_out, decoder_1_out0, decoder_1_out1, decoder_1_out2,
       decoder_1_out3;
  wire [7:0] R0_q, R1_q, R2_q, R3_q;

  Decoder #(.select(2)) decoder_1 (
    .out0(decoder_1_out0), .out1(decoder_1_out1), .out2(decoder_1_out2), .out3(decoder_1_out3),
    .sel(Write_Address));  // open: en
  and and_1 (and_1_out, Write_Enable, decoder_1_out0);
  and and_2 (and_2_out, Write_Enable, decoder_1_out1);
  and and_3 (and_3_out, Write_Enable, decoder_1_out2);
  and and_4 (and_4_out, Write_Enable, decoder_1_out3);
  Register R0 (.D(Write_Data), .en(and_1_out), .Q(R0_q), .clk(Clock));  // open: clr
  Register R1 (.D(Write_Data), .en(and_2_out), .Q(R1_q), .clk(Clock));  // open: clr
  Register R2 (.D(Write_Data), .en(and_3_out), .Q(R2_q), .clk(Clock));  // open: clr
  Register R3 (.D(Write_Data), .en(and_4_out), .Q(R3_q), .clk(Clock));  // open: clr
  Multiplexer #(.select(2), .width(8)) multiplexer_1 (
    .in0(R0_q), .in1(R1_q), .in2(R2_q), .in3(R3_q), .out(Read_Data_1), .sel(Read_Register_1));  // open: en
  Multiplexer #(.select(2), .width(8)) multiplexer_2 (
    .in0(R0_q), .in1(R1_q), .in2(R2_q), .in3(R3_q), .out(Read_Data_2), .sel(Read_Register_2));  // open: en
endmodule

module ALU (
  input  [7:0] Operand_A,
  input  [1:0] Operation_Select,
  input  [7:0] Operand_B,
  output [7:0] Result,
  output Branch,
  output Zero_Dectector
);

  wire comparator_1_gt, comparator_1_lt, not_1_out;
  wire [7:0] adder_1_out, bit_extender_1_out, subtractor_1_out, xor_1_out;

  assign xor_1_out = Operand_A ^ Operand_B;  // XOR_Gate xor_1, 8 bits wide
  Adder adder_1 (.a(Operand_A), .b(Operand_B), .out(adder_1_out));  // open: cin, cout
  Subtractor subtractor_1 (.a(Operand_A), .b(Operand_B), .out(subtractor_1_out));  // open: bin, bout
  Comparator comparator_1 (
    .a(Operand_A), .b({8{1'b0}}), .gt(comparator_1_gt), .eq(Zero_Dectector), .lt(comparator_1_lt));
  assign bit_extender_1_out = {{7{1'b0}}, comparator_1_lt};  // Bit_Extender bit_extender_1
  Multiplexer #(.select(2), .width(8), .enable("false")) multiplexer_1 (
    .in0(xor_1_out), .in1(adder_1_out), .in2(subtractor_1_out), .in3(bit_extender_1_out), .out(Result),
    .sel(Operation_Select));
  not not_1 (not_1_out, Zero_Dectector);
  Multiplexer #(.select(2), .enable("false")) multiplexer_2 (
    .in0(comparator_1_gt), .in1(Zero_Dectector), .in2(comparator_1_lt), .in3(not_1_out), .out(Branch),
    .sel(Operation_Select));
endmodule

module PC (
  input  [7:0] IMM,
  input  Jump,
  input  Clock,
  input  Zero,
  input  Branch_Instruction,
  output [7:0] Output
);

  wire and_1_out;
  wire [7:0] adder_1_out, adder_2_out, multiplexer_1_out, register_1_q, shifter_1_out;

  Adder adder_1 (.a(register_1_q), .b(8'h2), .out(adder_1_out));  // open: cin, cout
  Multiplexer #(.width(8), .enable("false")) multiplexer_1 (
    .in0(adder_1_out), .in1(IMM), .out(multiplexer_1_out), .sel(Jump));
  Register register_1 (.D(multiplexer_1_out), .Q(register_1_q), .clk(Clock));  // open: en, clr
  Adder adder_2 (.a(IMM), .b(register_1_q), .out(adder_2_out));  // open: cin, cout
  Shifter shifter_1 (.in(adder_2_out), .\dist (3'b001), .out(shifter_1_out));
  Multiplexer #(.width(8), .enable("false")) multiplexer_2 (
    .in0(register_1_q), .in1(shifter_1_out), .out(Output), .sel(and_1_out));
  and and_1 (and_1_out, Zero, Branch_Instruction);
endmodule

module Random (
  input  Clock,
  input  [7:0] RS,
  output [7:0] Result
);

  wire [7:0] rand_out, subtractor_1_out;

  Random_part \rand  (.clk(Clock), .next(1'b1), .out(rand_out));  // open: clr
  Subtractor subtractor_1 (.a(RS), .b(8'h1), .out(subtractor_1_out));  // open: bin, bout
  Divider divider_1 (.a(rand_out), .b(subtractor_1_out), .rem(Result));  // open: out, upper
endmodule

module Display_Driver (
  input  [7:0] Put_Data,
  input  Put_Enable,
  input  Clock,
  output [3:0] Hex0,
  output [3:0] Hex1
);

  Register #(.width(4)) register_1 (.D(Put_Data[3:0]), .en(Put_Enable), .Q(Hex0), .clk(Clock));  // open: clr
  Register #(.width(4)) register_2 (.D(Put_Data[7:4]), .en(Put_Enable), .Q(Hex1), .clk(Clock));  // open: clr
endmodule
